// Logisim project td4_cpu.circ as structural Verilog
module custom_74HC161 (
  input  A,
  input  B,
  input  C,
  input  D,
  input  LD,
  input  CK,
  output QA,
  output QB,
  output QC,
  output QD
);

  wire multiplexer_1_out, multiplexer_2_out, multiplexer_3_out, multiplexer_4_out, not_1_out;

  Multiplexer multiplexer_1 (.in0(QA), .in1(A), .out(multiplexer_1_out), .sel(not_1_out));
  Multiplexer multiplexer_2 (.in0(QB), .in1(B), .out(multiplexer_2_out), .sel(not_1_out));
  Multiplexer multiplexer_3 (.in0(QC), .in1(C), .out(multiplexer_3_out), .sel(not_1_out));
  Multiplexer multiplexer_4 (.in0(QD), .in1(D), .out(multiplexer_4_out), .sel(not_1_out));
  not not_1 (not_1_out, LD);
  D_Flip_Flop d_ff_1 (.D(multiplexer_1_out), .clk(CK), .Q(QA));  // open: Qn, preset, reset
  D_Flip_Flop d_ff_2 (.D(multiplexer_2_out), .clk(CK), .Q(QB));  // open: Qn, preset, reset
  D_Flip_Flop d_ff_3 (.D(multiplexer_3_out), .clk(CK), .Q(QC));  // open: Qn, preset, reset
  D_Flip_Flop d_ff_4 (.D(multiplexer_4_out), .clk(CK), .Q(QD));  // open: Qn, preset, reset
endmodule
