// Logisim project temp.circ as structural Verilog: 1 circuit, main circuit main
module main (
  input  in_1
);

  wire d_ff_1_q, not_1_out;

  not not_1 (not_1_out, d_ff_1_q);
  D_Flip_Flop d_ff_1 (.D(not_1_out), .clk(in_1), .Q(d_ff_1_q));  // open: Qn, preset, reset
endmodule
